# Fritzing sketch wiring (saved by Fritzing 0.9.2b)

parts:
  J1 = male pin header, 7 pins [form="♂ (male)"]
  J2 = male pin header, 7 pins [form="♂ (male)"]
  J3 = male pin header, 7 pins [form="♂ (male)"]
  Pro_Micro1 = Pro Micro
  CONN1 = USB connector [package=THT]
  S2 = Pushbutton [package=THT]

nets:
  N1: J1.pin1, Pro_Micro1.D8
  N2: J1.pin2, Pro_Micro1.D9
  N3: J1.pin3, Pro_Micro1.D10
  N4: J1.pin4, Pro_Micro1.D16/MOSI
  N5: J1.pin5, Pro_Micro1.D14/MISO
  N6: J1.pin6, Pro_Micro1.D15/SCLK
  N7: J2.pin7, CONN1.5V
  GND: J3.pin7, Pro_Micro1.GND, CONN1.GND, CONN1.chassis5, CONN1.chassis6, S2.leg0
  N8: Pro_Micro1.D19/A1, S2.leg1

notes:
  - + S

custom parts:
  Pro Micro: The SparkFun Pro Micro is a complete USB-based microcontoller development system, in a very small footprint, capable of implementing many types of projects. All programming can be done via the USB port.
